// Logisim project da1_task1.circ as structural Verilog: 2 circuits, main circuit DUT
module DUT (
  input  [15:0] A,
  input  [15:0] B,
  output [15:0] DOUT,
  output AWON
);

  wire adder_29_cout, adder_30_cout, comparator_1_lt, nand_1_out, not_1_out, not_2_out, not_3_out;
  wire [1:0] adder_1_out, adder_2_out, adder_3_out, adder_4_out, adder_5_out, adder_6_out, adder_7_out,
       adder_8_out, adder_9_out, adder_10_out, adder_11_out, adder_12_out, adder_13_out, adder_14_out,
       adder_15_out, adder_16_out, adder_17_out, adder_18_out, adder_19_out, adder_20_out, adder_21_out,
       adder_22_out, adder_23_out, adder_24_out;
  wire [2:0] adder_25_out, adder_26_out, adder_27_out, adder_28_out;
  wire [2:2] adder_17_cout, adder_18_cout, adder_19_cout, adder_20_cout, adder_21_cout, adder_22_cout,
       adder_23_cout, adder_24_cout;
  wire [3:0] adder_29_out, adder_30_out;
  wire [3:3] adder_25_cout, adder_26_cout, adder_27_cout, adder_28_cout;

  Adder #(.width(1)) adder_1 (.a(A[0]), .b(A[1]), .out(adder_1_out[0]), .cout(adder_1_out[1]));  // open: cin
  Adder #(.width(1)) adder_2 (.a(A[2]), .b(A[3]), .out(adder_2_out[0]), .cout(adder_2_out[1]));  // open: cin
  Adder #(.width(1)) adder_3 (.a(A[4]), .b(A[5]), .out(adder_3_out[0]), .cout(adder_3_out[1]));  // open: cin
  Adder #(.width(1)) adder_4 (.a(A[6]), .b(A[7]), .out(adder_4_out[0]), .cout(adder_4_out[1]));  // open: cin
  Adder #(.width(1)) adder_5 (.a(A[8]), .b(A[9]), .out(adder_5_out[0]), .cout(adder_5_out[1]));  // open: cin
  Adder #(.width(1)) adder_6 (.a(A[10]), .b(A[11]), .out(adder_6_out[0]), .cout(adder_6_out[1]));  // open: cin
  Adder #(.width(1)) adder_7 (.a(A[12]), .b(A[13]), .out(adder_7_out[0]), .cout(adder_7_out[1]));  // open: cin
  Adder #(.width(1)) adder_8 (.a(A[14]), .b(A[15]), .out(adder_8_out[0]), .cout(adder_8_out[1]));  // open: cin
  Adder #(.width(1)) adder_9 (.a(B[0]), .b(B[1]), .out(adder_9_out[0]), .cout(adder_9_out[1]));  // open: cin
  Adder #(.width(1)) adder_10 (.a(B[2]), .b(B[3]), .out(adder_10_out[0]), .cout(adder_10_out[1]));  // open: cin
  Adder #(.width(1)) adder_11 (.a(B[4]), .b(B[5]), .out(adder_11_out[0]), .cout(adder_11_out[1]));  // open: cin
  Adder #(.width(1)) adder_12 (.a(B[6]), .b(B[7]), .out(adder_12_out[0]), .cout(adder_12_out[1]));  // open: cin
  Adder #(.width(1)) adder_13 (.a(B[8]), .b(B[9]), .out(adder_13_out[0]), .cout(adder_13_out[1]));  // open: cin
  Adder #(.width(1)) adder_14 (.a(B[10]), .b(B[11]), .out(adder_14_out[0]), .cout(adder_14_out[1]));  // open: cin
  Adder #(.width(1)) adder_15 (.a(B[12]), .b(B[13]), .out(adder_15_out[0]), .cout(adder_15_out[1]));  // open: cin
  Adder #(.width(1)) adder_16 (.a(B[14]), .b(B[15]), .out(adder_16_out[0]), .cout(adder_16_out[1]));  // open: cin
  Adder #(.width(2)) adder_17 (
    .a(adder_1_out), .b(adder_2_out), .out(adder_17_out), .cout(adder_17_cout[2]));  // open: cin
  Adder #(.width(2)) adder_18 (
    .a(adder_3_out), .b(adder_4_out), .out(adder_18_out), .cout(adder_18_cout[2]));  // open: cin
  Adder #(.width(2)) adder_19 (
    .a(adder_5_out), .b(adder_6_out), .out(adder_19_out), .cout(adder_19_cout[2]));  // open: cin
  Adder #(.width(2)) adder_20 (
    .a(adder_7_out), .b(adder_8_out), .out(adder_20_out), .cout(adder_20_cout[2]));  // open: cin
  Adder #(.width(2)) adder_21 (
    .a(adder_9_out), .b(adder_10_out), .out(adder_21_out), .cout(adder_21_cout[2]));  // open: cin
  Adder #(.width(2)) adder_22 (
    .a(adder_11_out), .b(adder_12_out), .out(adder_22_out), .cout(adder_22_cout[2]));  // open: cin
  Adder #(.width(2)) adder_23 (
    .a(adder_13_out), .b(adder_14_out), .out(adder_23_out), .cout(adder_23_cout[2]));  // open: cin
  Adder #(.width(2)) adder_24 (
    .a(adder_15_out), .b(adder_16_out), .out(adder_24_out), .cout(adder_24_cout[2]));  // open: cin
  Adder #(.width(3)) adder_25 (
    .a({adder_17_cout[2], adder_17_out}), .b({adder_18_cout[2], adder_18_out}), .out(adder_25_out),
    .cout(adder_25_cout[3]));  // open: cin
  Adder #(.width(3)) adder_26 (
    .a({adder_19_cout[2], adder_19_out}), .b({adder_20_cout[2], adder_20_out}), .out(adder_26_out),
    .cout(adder_26_cout[3]));  // open: cin
  Adder #(.width(3)) adder_27 (
    .a({adder_21_cout[2], adder_21_out}), .b({adder_22_cout[2], adder_22_out}), .out(adder_27_out),
    .cout(adder_27_cout[3]));  // open: cin
  Adder #(.width(3)) adder_28 (
    .a({adder_23_cout[2], adder_23_out}), .b({adder_24_cout[2], adder_24_out}), .out(adder_28_out),
    .cout(adder_28_cout[3]));  // open: cin
  Adder #(.width(4)) adder_29 (
    .a({adder_25_cout[3], adder_25_out}), .b({adder_26_cout[3], adder_26_out}), .out(adder_29_out),
    .cout(adder_29_cout));  // open: cin
  not not_1 (not_1_out, comparator_1_lt);
  not not_2 (not_2_out, adder_30_cout);
  Adder #(.width(4)) adder_30 (
    .a({adder_27_cout[3], adder_27_out}), .b({adder_28_cout[3], adder_28_out}), .out(adder_30_out),
    .cout(adder_30_cout));  // open: cin
  Comparator #(.mode("unsigned"), .width(4)) comparator_1 (
    .a(adder_29_out), .b(adder_30_out), .lt(comparator_1_lt));  // open: gt, eq
  not not_3 (not_3_out, adder_29_cout);
  nand nand_1 (nand_1_out, not_1_out, not_2_out);
  Multiplexer #(.width(16)) multiplexer_1 (.in0(B), .in1(A), .out(DOUT), .sel(AWON));
  nand nand_2 (AWON, not_3_out, nand_1_out);

  // Notes on the sheet:
  //   Please put your deisgn below. You may also use subcircuits.
  //   However, do not move or rename any pins.
endmodule

module TB (
  input  [15:0] A,
  input  [15:0] B,
  output [15:0] DOUT,
  output AWON
);

  DUT dut_1 (.A(A), .B(B), .DOUT(DOUT), .AWON(AWON));

  // Notes on the sheet:
  //   DO NOT MODIFY THIS
  //   TEST YOUR CIRCUITS USING THIS TO MAKE SURE YOU HAVE NOT ALTERED PIN OUT
endmodule
