// Logisim project da1_task3.circ as structural Verilog: 3 circuits, main circuit DUT
module DUT (
  input  X,
  input  CLK,
  input  RST,
  output Z
);

  wire nand_2_out, nand_3_out, nand_4_out, nand_5_out, nand_6_out, nand_7_out, nand_8_out, nand_9_out,
       nand_10_out, nand_11_out, nand_12_out, nand_13_out, nand_14_out, nand_15_out, nand_16_out,
       nand_17_out, nand_18_out, nand_19_out, nand_20_out, nand_21_out, nand_22_out, nand_23_out,
       nand_24_out, nand_25_out, nand_26_out, nand_27_out, nand_28_out, nand_29_out, nand_30_out,
       nand_31_out, nand_32_out, nand_33_out, nand_34_out, nand_35_out, nand_36_out, nand_37_out,
       nand_38_out, nand_39_out, nand_40_out, nand_41_out, nand_42_out, nand_43_out, nand_44_out,
       nand_45_out, nand_46_out, nand_47_out, nand_48_out, nand_49_out, nand_50_out, nand_51_out,
       nand_52_out, nand_53_out, nand_54_out, nand_55_out, nand_56_out, nand_57_out, nand_58_out,
       nand_59_out, nand_60_out, nand_61_out, nand_62_out, nand_63_out, nand_64_out, nand_65_out,
       nand_66_out, nand_67_out, nand_68_out, nand_69_out, nand_70_out, nand_71_out, nand_72_out,
       nand_73_out, nand_74_out, nand_75_out, nand_76_out, nand_77_out, nand_78_out, nand_79_out,
       nand_80_out, nand_81_out, nand_82_out, nand_83_out, nand_84_out, nand_85_out, nand_86_out,
       nand_87_out, nand_88_out, nand_89_out, nand_90_out, nand_91_out, nand_92_out, nand_93_out,
       nand_94_out, nand_95_out, nand_96_out, nand_98_out, nand_100_out, nand_101_out, nand_103_out,
       nand_104_out, nand_106_out, not_1_out, not_3_out, not_4_out, not_5_out, not_6_out, not_8_out,
       not_9_out, not_10_out, not_11_out, t_ff_4_qn, t_ff_5_qn;
  wire [1:0] curmod;
  wire [2:0] bit_extender_1_out, cursum, nand_1_out, negcursum, not_2_out, nxtsum;

  not not_1 (not_1_out, RST);
  assign bit_extender_1_out = {{2{not_1_out}}, not_1_out};  // Bit_Extender bit_extender_1
  assign nand_1_out = ~(nxtsum & bit_extender_1_out);  // NAND_Gate nand_1, 3 bits wide
  assign not_2_out = ~nand_1_out;  // NOT_Gate not_2, 3 bits wide
  not not_3 (not_3_out, not_2_out[2]);
  not not_4 (not_4_out, not_2_out[1]);
  not not_5 (not_5_out, not_2_out[0]);
  nand nand_2 (nand_2_out, cursum[0], nand_3_out);
  nand nand_3 (nand_3_out, cursum[0], curmod[0]);
  nand nand_4 (nand_4_out, nand_3_out, curmod[0]);
  nand nand_5 (nand_5_out, cursum[1], nand_6_out);
  nand nand_6 (nand_6_out, cursum[1], curmod[1]);
  nand nand_7 (nand_7_out, nand_6_out, curmod[1]);
  nand nand_8 (nand_8_out, cursum[2], nand_9_out);
  nand nand_9 (nand_9_out, cursum[2], 1'b0);
  nand nand_10 (nand_10_out, nand_9_out, 1'b0);
  nand nand_11 (nand_11_out, not_3_out, cursum[2]);
  nand nand_12 (nand_12_out, not_2_out[2], negcursum[2]);
  nand nand_13 (nand_13_out, not_4_out, cursum[1]);
  nand nand_14 (nand_14_out, not_2_out[1], negcursum[1]);
  nand nand_15 (nand_15_out, not_5_out, cursum[0]);
  nand nand_16 (nand_16_out, nand_15_out, nand_17_out);
  nand nand_17 (nand_17_out, not_2_out[0], negcursum[0]);
  nand nand_18 (nand_18_out, nand_2_out, nand_4_out);
  nand nand_19 (nand_19_out, nand_18_out, 1'b1);
  nand nand_20 (nand_20_out, nand_5_out, nand_7_out);
  nand nand_21 (nand_21_out, nand_20_out, nand_30_out);
  nand nand_22 (nand_22_out, nand_8_out, nand_10_out);
  nand nand_23 (nand_23_out, nand_22_out, nand_34_out);
  nand nand_24 (nand_24_out, negcursum[0], negcursum[1]);
  T_Flip_Flop t_ff_1 (.T(nand_25_out), .clk(CLK), .Q(cursum[2]), .Qn(negcursum[2]));  // open: reset, preset
  nand nand_25 (nand_25_out, nand_11_out, nand_12_out);
  T_Flip_Flop t_ff_2 (.T(nand_26_out), .clk(CLK), .Q(cursum[1]), .Qn(negcursum[1]));  // open: reset, preset
  nand nand_26 (nand_26_out, nand_13_out, nand_14_out);
  T_Flip_Flop t_ff_3 (.T(nand_16_out), .clk(CLK), .Q(cursum[0]), .Qn(negcursum[0]));  // open: reset, preset
  nand nand_27 (nand_27_out, nand_18_out, nand_19_out);
  nand nand_28 (nand_28_out, nand_27_out, nand_29_out);
  nand nand_29 (nand_29_out, nand_19_out, 1'b1);
  nand nand_30 (nand_30_out, nand_19_out, nand_3_out);
  nand nand_31 (nand_31_out, nand_20_out, nand_21_out);
  nand nand_32 (nand_32_out, nand_31_out, nand_33_out);
  nand nand_33 (nand_33_out, nand_21_out, nand_30_out);
  nand nand_34 (nand_34_out, nand_21_out, nand_6_out);
  nand nand_35 (nand_35_out, nand_22_out, nand_23_out);
  nand nand_36 (nand_36_out, nand_35_out, nand_37_out);
  nand nand_37 (nand_37_out, nand_23_out, nand_34_out);
  nand nand_38 (nand_38_out, nand_23_out, nand_9_out);
  not not_6 (not_6_out, nand_24_out);
  nand nand_39 (nand_39_out, not_6_out, negcursum[2]);
  nand nand_40 (nand_40_out, nand_28_out, 1'b0);
  nand nand_41 (nand_41_out, nand_32_out, 1'b0);
  nand nand_42 (nand_42_out, nand_36_out, 1'b0);
  not not_7 (Z, nand_39_out);
  nand nand_43 (nand_43_out, nand_28_out, nand_40_out);
  nand nand_44 (nand_44_out, nand_40_out, 1'b0);
  nand nand_45 (nand_45_out, nand_32_out, nand_41_out);
  nand nand_46 (nand_46_out, nand_41_out, 1'b0);
  nand nand_47 (nand_47_out, nand_36_out, nand_42_out);
  nand nand_48 (nand_48_out, nand_42_out, 1'b0);
  nand nand_49 (nand_49_out, nand_43_out, nand_44_out);
  nand nand_50 (nand_50_out, nand_49_out, nand_38_out);
  nand nand_51 (nand_51_out, nand_45_out, nand_46_out);
  nand nand_52 (nand_52_out, nand_51_out, nand_60_out);
  nand nand_53 (nand_53_out, nand_47_out, nand_48_out);
  nand nand_54 (nand_54_out, nand_53_out, nand_64_out);
  nand nand_55 (nand_55_out, t_ff_4_qn, t_ff_5_qn);
  nand nand_56 (nand_56_out, curmod[0], curmod[1]);
  nand nand_57 (nand_57_out, nand_49_out, nand_50_out);
  nand nand_58 (nand_58_out, nand_57_out, nand_59_out);
  nand nand_59 (nand_59_out, nand_50_out, nand_38_out);
  nand nand_60 (nand_60_out, nand_50_out, nand_40_out);
  nand nand_61 (nand_61_out, nand_51_out, nand_52_out);
  nand nand_62 (nand_62_out, nand_61_out, nand_63_out);
  nand nand_63 (nand_63_out, nand_52_out, nand_60_out);
  nand nand_64 (nand_64_out, nand_52_out, nand_41_out);
  nand nand_65 (nand_65_out, nand_53_out, nand_54_out);
  nand nand_66 (nand_66_out, nand_65_out, nand_67_out);
  nand nand_67 (nand_67_out, nand_54_out, nand_64_out);
  nand nand_68 (nand_68_out, nand_54_out, nand_42_out);
  nand nand_69 (nand_69_out, RST, CLK);
  not not_8 (not_8_out, nand_69_out);
  T_Flip_Flop t_ff_4 (.T(curmod[0]), .clk(CLK), .Q(curmod[1]), .Qn(t_ff_4_qn), .reset(not_8_out));  // open: preset
  T_Flip_Flop t_ff_5 (.T(nand_70_out), .clk(CLK), .Q(curmod[0]), .Qn(t_ff_5_qn), .reset(not_8_out));  // open: preset
  nand nand_70 (nand_70_out, nand_55_out, nand_56_out);
  nand nand_71 (nand_71_out, nand_58_out, nand_72_out);
  nand nand_72 (nand_72_out, nand_58_out, 1'b0);
  nand nand_73 (nand_73_out, nand_72_out, 1'b0);
  nand nand_74 (nand_74_out, nand_62_out, nand_75_out);
  nand nand_75 (nand_75_out, nand_62_out, 1'b0);
  nand nand_76 (nand_76_out, nand_75_out, 1'b0);
  nand nand_77 (nand_77_out, nand_66_out, nand_78_out);
  nand nand_78 (nand_78_out, nand_66_out, 1'b0);
  nand nand_79 (nand_79_out, nand_78_out, 1'b0);
  nand nand_80 (nand_80_out, nand_81_out, nand_68_out);
  nand nand_81 (nand_81_out, nand_71_out, nand_73_out);
  nand nand_82 (nand_82_out, nand_83_out, nand_89_out);
  nand nand_83 (nand_83_out, nand_74_out, nand_76_out);
  nand nand_84 (nand_84_out, nand_85_out, nand_93_out);
  nand nand_85 (nand_85_out, nand_77_out, nand_79_out);
  nand nand_86 (nand_86_out, nand_81_out, nand_80_out);
  nand nand_87 (nand_87_out, nand_86_out, nand_88_out);
  nand nand_88 (nand_88_out, nand_80_out, nand_68_out);
  nand nand_89 (nand_89_out, nand_80_out, nand_72_out);
  nand nand_90 (nand_90_out, nand_83_out, nand_82_out);
  nand nand_91 (nand_91_out, nand_90_out, nand_92_out);
  nand nand_92 (nand_92_out, nand_82_out, nand_89_out);
  nand nand_93 (nand_93_out, nand_82_out, nand_75_out);
  nand nand_94 (nand_94_out, nand_85_out, nand_84_out);
  nand nand_95 (nand_95_out, nand_94_out, nand_96_out);
  nand nand_96 (nand_96_out, nand_84_out, nand_93_out);
  // NAND_Gate nand_97 has open pins: in0=nand_84_out, in1=nand_78_out, out=open
  not not_9 (not_9_out, X);
  not not_10 (not_10_out, X);
  not not_11 (not_11_out, X);
  nand nand_98 (nand_98_out, X, nand_87_out);
  nand nand_99 (nxtsum[0], nand_98_out, nand_100_out);
  nand nand_100 (nand_100_out, not_9_out, cursum[0]);
  nand nand_101 (nand_101_out, X, nand_91_out);
  nand nand_102 (nxtsum[1], nand_101_out, nand_103_out);
  nand nand_103 (nand_103_out, not_10_out, cursum[1]);
  nand nand_104 (nand_104_out, X, nand_95_out);
  nand nand_105 (nxtsum[2], nand_104_out, nand_106_out);
  nand nand_106 (nand_106_out, not_11_out, cursum[2]);

  // Other names for the same wires on the sheet: o = Z

  // Notes on the sheet:
  //   Please put your deisgn below. You may also use subcircuits.
  //   However, do not move, rename, add, or delete any pins.
endmodule

module TB (
);

  wire clk_out, mypor_1_p2, not_1_out, or_1_out, RESET_out, TimeIndex_carry, undriven;
  wire [0:0] dut_1_z;
  wire [4:0] TimeIndex_q;

  Clock #(.highDuration(2), .lowDuration(2)) clk (.out(clk_out));
  Clock sysclk ();  // open: out
  Counter #(.max('h1f), .ongoal("stay"), .width(5)) TimeIndex (
    .load(or_1_out), .clk(clk_out), .D({5{1'b0}}), .carry(TimeIndex_carry), .Q(TimeIndex_q));  // open: clr, up, count
  // MyPOR mypor_1: pin names not known; wires that end beside it: clk_out, mypor_1_p2
  Button RESET (.out(RESET_out));
  ROM #(.addrWidth(5), .dataWidth(1)) TestTraceMemory (.addr(TimeIndex_q));  // open: data
  or or_1 (or_1_out, mypor_1_p2, RESET_out);
  not not_1 (not_1_out, TimeIndex_carry);
  DUT dut_1 (.X(undriven), .CLK(clk_out), .RST(or_1_out), .Z(dut_1_z[0]));
  TTY tty_1 (.data({6'b011000, dut_1_z[0]}), .clk(clk_out), .we(not_1_out), .clr(or_1_out));
  LED DONE (.in(TimeIndex_carry));

  // Notes on the sheet:
  //   DO NOT MODIFY THIS
  //   YOU MAY TEST YOUR CIRCUITS USING THIS TO MAKE SURE YOU HAVE NOT ALTERED PIN OUT
  //   Edit ROM with input trace of 32 bits
endmodule

module TBRANDOM (
);

  wire clk_out, mypor_1_p2, not_1_out, or_1_out, random_1_out, RESET_out, TimeIndex_carry;
  wire [0:0] dut_1_z;

  Clock #(.highDuration(2), .lowDuration(2)) clk (.out(clk_out));
  Clock sysclk ();  // open: out
  Counter #(.ongoal("stay")) TimeIndex (
    .load(or_1_out), .clk(clk_out), .D({8{1'b0}}), .carry(TimeIndex_carry));  // open: clr, up, count, Q
  // MyPOR mypor_1: pin names not known; wires that end beside it: clk_out, mypor_1_p2
  Button RESET (.out(RESET_out));
  or or_1 (or_1_out, mypor_1_p2, RESET_out);
  Random #(.width(1)) random_1 (.clr(or_1_out), .clk(clk_out), .out(random_1_out));  // open: next
  not not_1 (not_1_out, TimeIndex_carry);
  DUT dut_1 (.X(random_1_out), .CLK(clk_out), .RST(or_1_out), .Z(dut_1_z[0]));
  TTY tty_1 (.data({6'b011000, dut_1_z[0]}), .clk(clk_out), .we(not_1_out), .clr(or_1_out));
  LED DONE (.in(TimeIndex_carry));

  // Notes on the sheet:
  //   DO NOT MODIFY THIS
  //   YOU MAY TEST YOUR CIRCUITS USING THIS TO MAKE SURE YOU HAVE NOT ALTERED PIN OUT
endmodule
